// Logisim project Hw2-5 EtnaZeneli.circ as structural Verilog: 1 circuit, main circuit main
module main (
  input  in_1,
  input  in_2,
  input  in_3,
  input  in_4,
  input  in_5,
  input  in_6,
  input  in_7,
  input  in_8,
  input  in_9,
  input  in_10,
  input  in_11,
  input  in_12,
  input  in_13,
  input  in_14,
  input  in_15,
  input  in_16,
  input  in_17,
  input  in_18,
  input  in_19,
  input  in_20,
  input  in_21,
  input  in_22,
  input  in_23,
  input  in_24,
  input  in_25,
  input  in_26,
  input  in_27,
  input  in_28,
  input  in_29,
  input  in_30,
  input  in_31,
  input  in_32,
  output out_33,
  output out_34,
  output out_35,
  output out_36
);

  ExactlyOne xor_1 (
    .out(out_34), .in0(in_1), .in1(in_3), .in2(in_5), .in3(in_7), .in4(in_9), .in5(in_11), .in6(in_13),
    .in7(in_15));
  NotExactlyOne xnor_1 (
    .out(out_36), .in0(in_17), .in1(in_21), .in2(in_24), .in3(in_26), .in4(in_29), .in5(in_30), .in6(in_31),
    .in7(in_32));
  xor odd_parity_1 (out_33, in_2, in_4, in_6, in_8, in_10, in_12, in_14, in_16);
  xnor even_parity_1 (out_35, in_18, in_19, in_20, in_22, in_23, in_25, in_27, in_28);
endmodule
